# Fritzing sketch laserJigSch (saved by Fritzing 0.9.5d)

parts:
  Pro_Micro1 = SparkFun Pro Micro
  R1 = PHOTOCELL [package=photocell-kit]
  R2 = Resistor [tolerance=±5% resistance=2.2k package="0805 [SMD]"]
  R3 = PHOTOCELL [package=photocell-kit]
  R4 = Resistor [tolerance=±5% resistance=2.2k package="0805 [SMD]"]
  R5 = Resistor [tolerance=±5% resistance=1k package="0805 [SMD]"]
  LD1 = LD
  LD2 = LD
  R6 = Resistor [tolerance=±5% resistance=1k package="0805 [SMD]"]
  S1 = Pushbutton [package=THT]

nets:
  N1: Pro_Micro1.GND, R1.P$1, R3.P$1, LD1.cathode, LD2.cathode
  N2: Pro_Micro1.5, LD2.anode, R6.Pin_1
  N3: Pro_Micro1.6, R5.Pin_1
  N4: Pro_Micro1.7, R5.Pin_0, LD1.anode
  N5: Pro_Micro1.8, S1.leg0
  N6: Pro_Micro1.9, S1.leg1
  N7: Pro_Micro1.A2, R4.Pin_0
  N8: Pro_Micro1.A3, R1.P$2, R2.Pin_0
  N9: Pro_Micro1.VCC, R2.Pin_1, R4.Pin_1

custom parts:
  SparkFun Pro Micro: The Pro Micro is similar to the Pro Mini except with an ATmega32U4 on board. The USB transceiver inside the 32U4 allows us to add USB connectivity on-board and do away with bulky external USB interface. Based on: https://github.com/unorthodox-engineers/unorthodox-arduino/blob/master/Unorthodox/fritzing/parts/Pro%20Micro.fzpz
  LD: A Generic Red Dot Laser Diode Module (~5mW)
